// Logisim project ALU.circ as structural Verilog: 2 circuits, main circuit main
module main (
  input  CS2,
  input  CS1,
  input  CS0,
  input  in_4,
  input  en1,
  input  A1_always_1,
  input  B1,
  input  B3,
  input  B2,
  input  B1_2,
  input  B0,
  input  A3,
  input  A2,
  input  A1,
  input  A0,
  output S21,
  output en2,
  output Cin,
  output S10,
  output S11,
  output out_21,
  output out_22,
  output V,
  output Z,
  output Cout,
  output Sign,
  output X3,
  output X2,
  output X1,
  output S3,
  output S2,
  output X0,
  output S1,
  output Y3,
  output Y2,
  output S0,
  output Y1,
  output Y0,
  output S1_unnecessary
);

  wire _1_0_p3, _1_0_p4, _1_0_p12, _1_0_p13, _3_2_p3, _3_2_p4, _3_2_p12, _3_2_p13, _3_bit__14_cout,
       n7404_1_p2, n7404_1_p4, n7404_1_p6, n7404_1_p11, n7404_1_p13, n7404_1_p15, n7404_2_p9, n7408_1_p1,
       n7408_1_p11, n7408_1_p14, n7432_2_p3, n7432_2_p6, n74157_1_p3, n74157_1_p6, n74157_1_p12, n74157_1_p15;

  // _7404 7404_1: pin names not known; wires that end beside it: CS1, n7404_1_p2, CS0, n7404_1_p4, A3, n7404_1_p6, 1'b0, 1'b1, 1'b1, A2, n7404_1_p11, A1, n7404_1_p13, A0, n7404_1_p15
  // _74153 _3_2: pin names not known; wires that end beside it: en1, S11, _3_2_p3, _3_2_p4, n7404_1_p6, A3, X3, 1'b0, 1'b1, en1, S10, _3_2_p12, _3_2_p13, n7404_1_p11, A2, X2
  // _74153 _1_0: pin names not known; wires that end beside it: en1, S11, _1_0_p3, _1_0_p4, n7404_1_p13, A1, X1, 1'b0, 1'b1, en1, S10, _1_0_p12, _1_0_p13, n7404_1_p15, A0, X0
  // _7408 7408_1: pin names not known; wires that end beside it: n7408_1_p1, CS2, S10, n7404_1_p2, CS0, S11, 1'b0, 1'b1, n7404_1_p4, n7404_1_p2, n7408_1_p11, CS2, CS1, n7408_1_p14
  // _7432 7432_1: pin names not known; wires that end beside it: CS1, CS0, n7408_1_p1, S11, CS2, en2, 1'b0, 1'b1, n7408_1_p11, n7408_1_p14, Cin
  // _7408 7408_2: pin names not known; wires that end beside it: A3, B3, _3_2_p3, A2, B2, _3_2_p12, 1'b0, 1'b1, A1, B1_2, _1_0_p3, A0, B0, _1_0_p12
  // _7486 7486_1: pin names not known; wires that end beside it: A3, B3, _3_2_p4, A2, B2, _3_2_p13, 1'b0, 1'b1, A1, B1_2, _1_0_p4, A0, B0, _1_0_p13
  // _74157 74157_1: pin names not known; wires that end beside it: CS1, B3, n74157_1_p3, Y3, B2, n74157_1_p6, Y2, 1'b0, 1'b1, en2, B0, n74157_1_p12, Y0, B1_2, n74157_1_p15, Y1
  // _7404 7404_2: pin names not known; wires that end beside it: B3, n74157_1_p3, B2, n74157_1_p6, B1_2, n74157_1_p15, B0, n74157_1_p12, n7404_2_p9, Z
  Adder _1_bit (
    ._1__A4(Cout), ._2__S3(out_21), ._3__A3(in_4), ._4__B3(in_4), ._5__Vcc(1'b1), ._6__S2(Cout),
    ._7__B2(in_4), ._8__A2(in_4), ._16__B4(_3_bit__14_cout), ._15__S4(V), ._14_Cout(out_22),
    ._13__Cin(_3_bit__14_cout), ._12__GND(1'b0), ._11__B1(Y3), ._10__A1(X3), ._9__S1(S3));
  Adder _3_bit (
    ._1__A4(X2), ._2__S3(S1), ._3__A3(X1), ._4__B3(Y1), ._5__Vcc(1'b1), ._6__S2(S0), ._7__B2(Y0),
    ._8__A2(X0), ._16__B4(Y2), ._15__S4(S2), ._14_Cout(_3_bit__14_cout), ._13__Cin(Cin), ._12__GND(1'b0),
    ._11__B1(B1), ._10__A1(A1_always_1), ._9__S1(S1_unnecessary));
  // _7432 7432_2: pin names not known; wires that end beside it: S3, S2, n7432_2_p3, n7432_2_p3, S1, n7432_2_p6, n7432_2_p6, S0, n7404_2_p9

  assign S21 = CS1;
  assign Sign = S3;

  // Notes on the sheet:
  //   cs1'cs0
  //   CS0+CS1
  //   cs1'cs0'
  //   cs2cs1
  //   A2B2
  //   A3B3
  //   A0B0
  //   A1B1
endmodule

// adder
module Adder (
  input  _1__A4,
  input  _16__B4,
  input  _3__A3,
  input  _4__B3,
  input  _13__Cin,
  input  _5__Vcc,
  input  _12__GND,
  input  _11__B1,
  input  _7__B2,
  input  _10__A1,
  input  _8__A2,
  output _2__S3,
  output _15__S4,
  output _14_Cout,
  output _6__S2,
  output _9__S1
);

  wire and_1_out, and_2_out, and_3_out, and_4_out, and_5_out, and_6_out, and_7_out, and_8_out, and_9_out,
       and_10_out, and_11_out, and_12_out, and_13_out, and_14_out, nand_1_out, nand_2_out, nand_3_out,
       nand_4_out, nor_1_out, nor_2_out, nor_3_out, nor_4_out, nor_6_out, nor_7_out, nor_8_out, not_1_out,
       not_2_out, not_3_out, not_4_out, not_5_out, not_6_out;

  nand nand_1 (nand_1_out, _16__B4, _1__A4);
  nor nor_1 (nor_1_out, _16__B4, _1__A4);
  nand nand_2 (nand_2_out, _4__B3, _3__A3);
  nor nor_2 (nor_2_out, _4__B3, _3__A3);
  nand nand_3 (nand_3_out, _7__B2, _8__A2);
  nor nor_3 (nor_3_out, _7__B2, _8__A2);
  nand nand_4 (nand_4_out, _11__B1, _10__A1);
  nor nor_4 (nor_4_out, _11__B1, _10__A1);
  and and_1 (and_1_out, nor_2_out, nand_1_out);
  and and_2 (and_2_out, nor_3_out, nand_1_out, nand_2_out);
  and and_3 (and_3_out, nor_4_out, nand_1_out, nand_2_out, nand_3_out);
  and and_4 (and_4_out, nand_1_out, nand_2_out, nand_3_out, nand_4_out, not_2_out);
  not not_1 (not_1_out, nor_1_out);
  and and_5 (and_5_out, nor_3_out, nand_2_out);
  and and_6 (and_6_out, nor_4_out, nand_2_out, nand_3_out);
  and and_7 (and_7_out, nand_2_out, nand_3_out, nand_4_out, not_2_out);
  not not_2 (not_2_out, _13__Cin);
  not not_3 (not_3_out, nor_2_out);
  and and_8 (and_8_out, nor_4_out, nand_3_out);
  and and_9 (and_9_out, nand_3_out, nand_4_out, not_2_out);
  not not_4 (not_4_out, nor_3_out);
  and and_10 (and_10_out, nand_4_out, not_2_out);
  not not_5 (not_5_out, nor_4_out);
  not not_6 (not_6_out, not_2_out);
  nor nor_5 (_14_Cout, nor_1_out, and_1_out, and_2_out, and_3_out, and_4_out);
  and and_11 (and_11_out, nand_1_out, not_1_out);
  and and_12 (and_12_out, nand_2_out, not_3_out);
  and and_13 (and_13_out, nand_3_out, not_4_out);
  and and_14 (and_14_out, nand_4_out, not_5_out);
  xor xor_1 (_15__S4, and_11_out, nor_6_out);
  nor nor_6 (nor_6_out, nor_2_out, and_5_out, and_6_out, and_7_out);
  xor xor_2 (_2__S3, and_12_out, nor_7_out);
  nor nor_7 (nor_7_out, nor_3_out, and_8_out, and_9_out);
  xor xor_3 (_6__S2, and_13_out, nor_8_out);
  nor nor_8 (nor_8_out, nor_4_out, and_10_out);
  xor xor_4 (_9__S1, and_14_out, not_6_out);

  // Notes on the sheet:
  //   7483: 4-bit full adder
endmodule
