// Logisim project mips.circ as structural Verilog: 2 circuits, main circuit main
module main (
  input  in_1,
  input  in_2,
  output [19:0] out_3,
  output [7:0] out_4
);

  wire comparator_1_gt;
  wire [1:0] adder_1_out, register_1_q;
  wire [2:0] bit_extender_2_out;
  wire [7:0] alu_8_by_art_1_p2, bit_extender_1_out, register_2_read_data_1, register_2_read_data_2;

  Register_part #(.width(2)) register_1 (.D(adder_1_out), .Q(register_1_q), .clk(in_1));  // open: en, clr
  Adder #(.width(2)) adder_1 (.a(2'b01), .b(register_1_q), .out(adder_1_out));  // open: cin, cout
  ROM #(.addrWidth(2), .dataWidth(20)) rom_1 (.addr(register_1_q), .data(out_3));  // open: sel
  assign bit_extender_1_out = {{4{1'b0}}, out_3[3:0]};  // Bit_Extender bit_extender_1
  Register register_2 (
    .Write_Data(out_4), .Read_Data_1(register_2_read_data_1), .Read_Data_2(register_2_read_data_2),
    .RD(out_3[7:4]), .RegWrite(in_2), .CLK(in_1), .RS(out_3[15:12]), .RS_2(out_3[11:8]));  // open: CLR
  Comparator #(.width(4)) comparator_1 (.a(out_3[19:16]), .b(4'b0100), .gt(comparator_1_gt));  // open: eq, lt
  Bit_Extender #(.in_width(4), .out_width(3)) bit_extender_2 (.in(out_3[19:16]), .out(bit_extender_2_out));
  // ALU_8_by_ART alu_8_by_art_1: pin names not known; wires that end beside it: register_2_read_data_1, alu_8_by_art_1_p2, bit_extender_2_out, out_4
  Multiplexer #(.width(8), .enable("false")) multiplexer_1 (
    .in0(register_2_read_data_2), .in1(bit_extender_1_out), .out(alu_8_by_art_1_p2), .sel(comparator_1_gt));

  // Notes on the sheet:
  //   contents of rom_1 (hex, n*v repeats v):
  //   50102
endmodule

module Register (
  input  [7:0] Write_Data,
  input  [3:0] RS,
  input  [3:0] RD,
  input  [3:0] RS_2,
  input  RegWrite,
  input  CLK,
  input  CLR,
  output [7:0] Read_Data_1,
  output [7:0] Read_Data_2
);

  wire and_1_out, and_2_out, and_3_out, and_4_out, and_5_out, and_6_out, and_7_out, and_8_out, and_9_out,
       and_10_out, and_11_out, and_12_out, and_13_out, and_14_out, and_15_out, and_16_out, decoder_1_out0,
       decoder_1_out1, decoder_1_out2, decoder_1_out3, decoder_1_out4, decoder_1_out5, decoder_1_out6,
       decoder_1_out7, decoder_1_out8, decoder_1_out9, decoder_1_out10, decoder_1_out11, decoder_1_out12,
       decoder_1_out13, decoder_1_out14, decoder_1_out15;
  wire [7:0] register_1_q, register_2_q, register_3_q, register_4_q, register_5_q, register_6_q,
       register_7_q, register_8_q, register_9_q, register_10_q, register_11_q, register_12_q, register_13_q,
       register_14_q, register_15_q, register_16_q;

  Decoder #(.select(4)) decoder_1 (
    .out0(decoder_1_out0), .out1(decoder_1_out1), .out2(decoder_1_out2), .out3(decoder_1_out3),
    .out4(decoder_1_out4), .out5(decoder_1_out5), .out6(decoder_1_out6), .out7(decoder_1_out7),
    .out8(decoder_1_out8), .out9(decoder_1_out9), .out10(decoder_1_out10), .out11(decoder_1_out11),
    .out12(decoder_1_out12), .out13(decoder_1_out13), .out14(decoder_1_out14), .out15(decoder_1_out15),
    .sel(RD));  // open: en
  and and_1 (and_1_out, decoder_1_out0, RegWrite);
  and and_2 (and_2_out, decoder_1_out1, RegWrite);
  and and_3 (and_3_out, decoder_1_out2, RegWrite);
  and and_4 (and_4_out, decoder_1_out3, RegWrite);
  and and_5 (and_5_out, decoder_1_out4, RegWrite);
  and and_6 (and_6_out, decoder_1_out5, RegWrite);
  and and_7 (and_7_out, decoder_1_out6, RegWrite);
  and and_8 (and_8_out, decoder_1_out7, RegWrite);
  and and_9 (and_9_out, decoder_1_out8, RegWrite);
  and and_10 (and_10_out, decoder_1_out9, RegWrite);
  and and_11 (and_11_out, decoder_1_out10, RegWrite);
  and and_12 (and_12_out, decoder_1_out11, RegWrite);
  and and_13 (and_13_out, decoder_1_out12, RegWrite);
  and and_14 (and_14_out, decoder_1_out13, RegWrite);
  and and_15 (and_15_out, decoder_1_out14, RegWrite);
  and and_16 (and_16_out, decoder_1_out15, RegWrite);
  Register_part register_1 (.D(Write_Data), .en(and_1_out), .Q(register_1_q), .clk(CLK), .clr(CLR));
  Register_part register_2 (.D(Write_Data), .en(and_2_out), .Q(register_2_q), .clk(CLK), .clr(CLR));
  Register_part register_3 (.D(Write_Data), .en(and_3_out), .Q(register_3_q), .clk(CLK), .clr(CLR));
  Register_part register_4 (.D(Write_Data), .en(and_4_out), .Q(register_4_q), .clk(CLK), .clr(CLR));
  Register_part register_5 (.D(Write_Data), .en(and_5_out), .Q(register_5_q), .clk(CLK), .clr(CLR));
  Register_part register_6 (.D(Write_Data), .en(and_6_out), .Q(register_6_q), .clk(CLK), .clr(CLR));
  Register_part register_7 (.D(Write_Data), .en(and_7_out), .Q(register_7_q), .clk(CLK), .clr(CLR));
  Register_part register_8 (.D(Write_Data), .en(and_8_out), .Q(register_8_q), .clk(CLK), .clr(CLR));
  Register_part register_9 (.D(Write_Data), .en(and_9_out), .Q(register_9_q), .clk(CLK), .clr(CLR));
  Register_part register_10 (.D(Write_Data), .en(and_10_out), .Q(register_10_q), .clk(CLK), .clr(CLR));
  Register_part register_11 (.D(Write_Data), .en(and_11_out), .Q(register_11_q), .clk(CLK), .clr(CLR));
  Register_part register_12 (.D(Write_Data), .en(and_12_out), .Q(register_12_q), .clk(CLK), .clr(CLR));
  Register_part register_13 (.D(Write_Data), .en(and_13_out), .Q(register_13_q), .clk(CLK), .clr(CLR));
  Register_part register_14 (.D(Write_Data), .en(and_14_out), .Q(register_14_q), .clk(CLK), .clr(CLR));
  Register_part register_15 (.D(Write_Data), .en(and_15_out), .Q(register_15_q), .clk(CLK), .clr(CLR));
  Register_part register_16 (.D(Write_Data), .en(and_16_out), .Q(register_16_q), .clk(CLK), .clr(CLR));
  Multiplexer #(.select(4), .width(8)) multiplexer_1 (
    .in0(register_1_q), .in1(register_2_q), .in2(register_3_q), .in3(register_4_q), .in4(register_5_q),
    .in5(register_6_q), .in6(register_7_q), .in7(register_8_q), .in8(register_9_q), .in9(register_10_q),
    .in10(register_11_q), .in11(register_12_q), .in12(register_13_q), .in13(register_14_q),
    .in14(register_15_q), .in15(register_16_q), .out(Read_Data_1), .sel(RS));  // open: en
  Multiplexer #(.select(4), .width(8)) multiplexer_2 (
    .in0(register_1_q), .in1(register_2_q), .in2(register_3_q), .in3(register_4_q), .in4(register_5_q),
    .in5(register_6_q), .in6(register_7_q), .in7(register_8_q), .in8(register_9_q), .in9(register_10_q),
    .in10(register_11_q), .in11(register_12_q), .in12(register_13_q), .in13(register_14_q),
    .in14(register_15_q), .in15(register_16_q), .out(Read_Data_2), .sel(RS_2));  // open: en
endmodule
