// Logisim project mips_datapath.circ as structural Verilog: 8 circuits, main circuit main
module main (
  input  Clear_Everything,
  output [3:0] Opcode,
  output [7:0] PC,
  output [7:0] out_4,
  output [3:0] out_5,
  output [7:0] out_6,
  output [3:0] out_7,
  output [19:0] Read_Address,
  output [3:0] out_9,
  output [7:0] Read_Data_1,
  output [3:0] out_11,
  output [7:0] Read_Data_2,
  output [7:0] zero,
  output [7:0] Read_Data_2_2,
  output [7:0] sp,
  output [7:0] t0,
  output [7:0] t5,
  output [7:0] t1,
  output [7:0] t4,
  output [7:0] t2,
  output [7:0] Write_Data,
  output [7:0] t3
);

  wire alu_up_1_zero_flag, and_1_out, and_2_out, CLK_out, control_1_alusrc, control_1_beq, control_1_bneq,
       control_1_jump, control_1_memread, control_1_memtoreg, control_1_memwrite, control_1_regdst,
       control_1_regwrite, control_1_shift, not_1_out;
  wire [1:0] priority_encoder_1_out;
  wire [2:0] control_1_aluop;
  wire [7:0] adder_1_out, adder_2_out, multiplexer_5_out, ram_1_data;

  Clock CLK (.out(CLK_out));
  Register #(.trigger("falling")) register_1 (
    .D(multiplexer_5_out), .Q(PC), .clk(CLK_out), .clr(Clear_Everything));  // open: en
  Adder adder_1 (.a(PC), .b(8'h1), .out(adder_1_out), .cin(1'b0));  // open: cout
  ROM #(.dataWidth(20)) rom_1 (.addr(PC), .data({Opcode, out_9, out_5, Read_Address[7:4], out_11}));  // open: sel
  Multiplexer #(.width(4), .enable("false")) multiplexer_1 (
    .in0(out_5), .in1(Read_Address[7:4]), .out(out_7), .sel(control_1_regdst));
  Multiplexer #(.width(4), .enable("false")) multiplexer_2 (
    .in0(Read_Address[7:4]), .in1(4'b0000), .out(Read_Data_2[7:4]), .sel(control_1_shift));
  control control_1 (
    .OpCode(Opcode), .ALUOp(control_1_aluop), .ALUSrc(control_1_alusrc), .Bneq(control_1_bneq),
    .Beq(control_1_beq), .MemToReg(control_1_memtoreg), .MemWrite(control_1_memwrite),
    .MemRead(control_1_memread), .RegWrite(control_1_regwrite), .RegDst(control_1_regdst),
    .Shift(control_1_shift), .Jump(control_1_jump));
  register_file register_file_1 (
    .Read_Register_1(out_9), .Read_Register_2(out_5), .Write_Register(out_7), .Write_Data(Write_Data),
    .Write_Signal(control_1_regwrite), .CLK(CLK_out), .Clear(Clear_Everything), .zero(zero), .t0(t0),
    .t1(t1), .t2(t2), .t3(t3), .t4(t4), .t5(t5), .sp(sp), .Read_Data_1(Read_Data_1),
    .Read_Data_2(Read_Data_2_2));
  Multiplexer #(.width(8), .enable("false")) multiplexer_3 (
    .in0(Read_Data_2_2), .in1({Read_Data_2[7:4], out_11}), .out(out_4), .sel(control_1_alusrc));
  ALU_UP alu_up_1 (
    .A(Read_Data_1), .B(out_4), .ALU_OP(control_1_aluop), .Zero_Flag(alu_up_1_zero_flag), .Output(out_6));  // open: OverFlow
  Adder adder_2 (.a(adder_1_out), .b({Read_Data_2[7:4], out_11}), .out(adder_2_out));  // open: cin, cout
  and and_1 (and_1_out, control_1_bneq, not_1_out);
  not not_1 (not_1_out, alu_up_1_zero_flag);
  and and_2 (and_2_out, control_1_beq, alu_up_1_zero_flag);
  RAM #(.bus("separate")) ram_1 (
    .addr(out_6), .din(Read_Data_2_2), .data(ram_1_data), .str(control_1_memwrite), .clk(CLK_out),
    .ld(control_1_memread), .clr(Clear_Everything));  // open: sel
  Multiplexer #(.width(8), .enable("false")) multiplexer_4 (
    .in0(out_6), .in1(ram_1_data), .out(Write_Data), .sel(control_1_memtoreg));
  Priority_Encoder #(.select(2)) priority_encoder_1 (
    .in0(1'b1), .in1(and_1_out), .in2(and_2_out), .in3(control_1_jump), .out(priority_encoder_1_out));  // open: gs, en_out, en_in
  Multiplexer #(.select(2), .width(8), .enable("false")) multiplexer_5 (
    .in0(adder_1_out), .in1(adder_2_out), .in2(adder_2_out), .in3({out_9, out_5}), .out(multiplexer_5_out),
    .sel(priority_encoder_1_out));

  assign {Read_Address[19:8], Read_Address[3:0]} = {Opcode, out_9, out_5, out_11};
  assign Read_Data_2[3:0] = out_11;

  // Notes on the sheet:
  //   Clear CLK
  //   contents of rom_1 (hex, n*v repeats v):
  //   7020a 70305 c2310 c1340 c4150 53203 82021 e2401 a1500 65150 d2202 34041 13203 b2410 91530 a1400
  //   41105 23314 3330 a1500 f13fb
  //   Clear Register
  //   Data Memory
  //   Clear Memory
endmodule

// Register File
module register_file (
  input  [3:0] Read_Register_1,
  input  [3:0] Read_Register_2,
  input  [3:0] Write_Register,
  input  [7:0] Write_Data,
  input  Write_Signal,
  input  CLK,
  input  Clear,
  output [7:0] Read_Data_1,
  output [7:0] Read_Data_2,
  output [7:0] sp,
  output [7:0] zero,
  output [7:0] t5,
  output [7:0] t0,
  output [7:0] t4,
  output [7:0] t1,
  output [7:0] t2,
  output [7:0] t3
);

  wire and_1_out, and_2_out, and_3_out, and_4_out, and_5_out, and_6_out, and_7_out, and_8_out,
       decoder_1_out0, decoder_1_out1, decoder_1_out2, decoder_1_out3, decoder_1_out4, decoder_1_out5,
       decoder_1_out6, decoder_1_out7, multiplexer_1_out, multiplexer_3_out;
  wire [7:0] multiplexer_2_out;

  Decoder #(.select(4), .enable("false")) decoder_1 (
    .out0(decoder_1_out0), .out1(decoder_1_out1), .out2(decoder_1_out2), .out3(decoder_1_out3),
    .out4(decoder_1_out4), .out5(decoder_1_out5), .out6(decoder_1_out6), .out7(decoder_1_out7),
    .sel(Write_Register));  // open: out8, out9, out10, out11, out12, out13, out14, out15
  and and_1 (and_1_out, decoder_1_out0, 1'b0);
  and and_2 (and_2_out, decoder_1_out1, Write_Signal);
  and and_3 (and_3_out, decoder_1_out2, Write_Signal);
  and and_4 (and_4_out, decoder_1_out3, Write_Signal);
  and and_5 (and_5_out, decoder_1_out4, Write_Signal);
  and and_6 (and_6_out, decoder_1_out5, Write_Signal);
  and and_7 (and_7_out, decoder_1_out6, Write_Signal);
  and and_8 (and_8_out, decoder_1_out7, Write_Signal);
  Multiplexer #(.enable("false")) multiplexer_1 (.in0(and_8_out), .in1(Clear), .out(multiplexer_1_out), .sel(Clear));
  Multiplexer #(.width(8), .enable("false")) multiplexer_2 (
    .in0(Write_Data), .in1({8{1'b1}}), .out(multiplexer_2_out), .sel(Clear));
  Register u_zero (.D(Write_Data), .en(and_1_out), .Q(zero), .clk(CLK), .clr(Clear));
  Register u_t0 (.D(Write_Data), .en(and_2_out), .Q(t0), .clk(CLK), .clr(Clear));
  Register u_t1 (.D(Write_Data), .en(and_3_out), .Q(t1), .clk(CLK), .clr(Clear));
  Register u_t2 (.D(Write_Data), .en(and_4_out), .Q(t2), .clk(CLK), .clr(Clear));
  Register u_t3 (.D(Write_Data), .en(and_5_out), .Q(t3), .clk(CLK), .clr(Clear));
  Register u_t4 (.D(Write_Data), .en(and_6_out), .Q(t4), .clk(CLK), .clr(Clear));
  Register u_t5 (.D(Write_Data), .en(and_7_out), .Q(t5), .clk(CLK), .clr(Clear));
  Register u_sp (.D(multiplexer_2_out), .en(multiplexer_1_out), .Q(sp), .clk(multiplexer_3_out));  // open: clr
  Multiplexer #(.enable("false")) multiplexer_3 (.in0(CLK), .in1(Clear), .out(multiplexer_3_out), .sel(Clear));
  Multiplexer #(.select(4), .width(8), .enable("false")) multiplexer_4 (
    .in0(zero), .in1(t0), .in2(t1), .in3(t2), .in4(t3), .in5(t4), .in6(t5), .in7(sp), .out(Read_Data_1),
    .sel(Read_Register_1));  // open: in8, in9, in10, in11, in12, in13, in14, in15
  Multiplexer #(.select(4), .width(8), .enable("false")) multiplexer_5 (
    .in0(zero), .in1(t0), .in2(t1), .in3(t2), .in4(t3), .in5(t4), .in6(t5), .in7(sp), .out(Read_Data_2),
    .sel(Read_Register_2));  // open: in8, in9, in10, in11, in12, in13, in14, in15
endmodule

module instruction_memory (
  input  [3:0] PC,
  output [19:0] Instruction_0_19
);

  ROM #(.addrWidth(4), .dataWidth(20)) rom_1 (.addr(PC), .data(Instruction_0_19));  // open: sel

  // Notes on the sheet:
  //   contents of rom_1 (hex, n*v repeats v):
  //   0 ed d 1212 0 1 0 1 101
endmodule

module ALU (
  input  [7:0] A,
  input  [7:0] B,
  input  [2:0] ALUop,
  output overflow,
  output ZF,
  output negative,
  output [7:0] F
);

  wire [7:0] adder_1_out, and_1_out, nor_1_out, or_1_out, subtractor_1_out;
  wire [15:0] shifter_1_out, shifter_2_out;

  Adder adder_1 (.a(A), .b(B), .out(adder_1_out), .cin(1'b0), .cout(overflow));
  Subtractor subtractor_1 (.a(A), .b(B), .out(subtractor_1_out), .bin(1'b0), .bout(negative));
  assign or_1_out = A | B;  // OR_Gate or_1, 8 bits wide
  assign and_1_out = A & B;  // AND_Gate and_1, 8 bits wide
  assign nor_1_out = ~(A | B);  // NOR_Gate nor_1, 8 bits wide
  Shifter #(.width(16)) shifter_1 (.in({{8{1'b0}}, A}), .\dist (B[3:0]), .out(shifter_1_out));
  Shifter #(.width(16), .shift("lr")) shifter_2 (.in({{8{1'b0}}, A}), .\dist (B[3:0]), .out(shifter_2_out));
  Multiplexer #(.select(3), .width(8), .enable("false")) multiplexer_1 (
    .in0(adder_1_out), .in1(subtractor_1_out), .in2(or_1_out), .in3(and_1_out), .in4(nor_1_out),
    .in5(shifter_1_out[7:0]), .in6(shifter_2_out[7:0]), .in7({8{1'b0}}), .out(F), .sel(ALUop));
  nor nor_2 (ZF, F[0], F[1], F[2], F[3], F[4], F[5], F[6], F[7]);
endmodule

// Control
module control (
  input  [3:0] OpCode,
  output [2:0] ALUOp,
  output ALUSrc,
  output Bneq,
  output Beq,
  output MemToReg,
  output MemWrite,
  output MemRead,
  output RegWrite,
  output RegDst,
  output Shift,
  output Jump
);

  ROM #(.addrWidth(4), .dataWidth(13)) rom_1 (
    .addr(OpCode),
    .data({Jump, Shift, RegDst, RegWrite, MemRead, MemWrite, MemToReg, Beq, Bneq, ALUSrc, ALUOp}));  // open: sel

  // Notes on the sheet:
  //   contents of rom_1 (hex, n*v repeats v):
  //   604 348 20b e0e 20a 88 601 208 e0d 602 1000 603 600 209 21 11
endmodule

module Ins_memory (
  input  [3:0] PC,
  output [19:0] Instruction_0_19
);

  instruction_memory instruction_memory_1 (.PC(PC), .Instruction_0_19(Instruction_0_19));

  // Notes on the sheet:
  //   Instruction Memory
endmodule

module Data_memory (
  input  [7:0] Address,
  input  [7:0] Data_Input,
  input  Store,
  input  Chip_Select,
  input  Clock,
  input  Load,
  input  Clear,
  output [7:0] Data_Loaded
);

  RAM #(.bus("separate")) ram_1 (
    .addr(Address), .din(Data_Input), .data(Data_Loaded), .str(Store), .sel(Chip_Select), .clk(Clock),
    .ld(Load), .clr(Clear));

  // Notes on the sheet:
  //   Data Memory
endmodule

module ALU_UP (
  input  [7:0] A,
  input  [7:0] B,
  input  [2:0] ALU_OP,
  output Zero_Flag,
  output [7:0] Output,
  output OverFlow
);

  wire and_1_out, or_1_out;
  wire [7:0] multiplexer_1_out, multiplexer_2_out;

  Multiplexer #(.width(8), .enable("false")) multiplexer_1 (.in0(A), .in1(B), .out(multiplexer_1_out), .sel(and_1_out));
  Multiplexer #(.width(8), .enable("false")) multiplexer_2 (.in0(B), .in1(A), .out(multiplexer_2_out), .sel(and_1_out));
  or or_1 (or_1_out, ALU_OP[1], ALU_OP[0]);
  and and_1 (and_1_out, or_1_out, ALU_OP[2]);
  // ALU_8_by_ART alu_8_by_art_1: pin names not known; wires that end beside it: multiplexer_1_out, multiplexer_2_out, ALU_OP, Zero_Flag, Output, OverFlow
endmodule
